// Logisim project 24CS104_Experiment_4.circ as structural Verilog: 1 circuit, main circuit main
module main (
  input  D,
  input  J,
  input  K,
  output Q,
  output Q_prime,
  output Q_2,
  output Q_prime_2
);

  wire clock_1_out, clock_2_out, NAND_2_out, NAND_3_out, NAND_4_out, NAND_out, not_1_out;

  Clock clock_1 (.out(clock_1_out));
  Clock clock_2 (.out(clock_2_out));
  not not_1 (not_1_out, D);
  nand NAND (NAND_out, Q_prime, D, clock_1_out);
  nand NAND_2 (NAND_2_out, clock_1_out, not_1_out, Q);
  nand NAND_3 (NAND_3_out, Q_prime_2, J, clock_2_out);
  nand NAND_4 (NAND_4_out, clock_2_out, K, Q_2);
  nand NAND_5 (Q, NAND_out, Q_prime);
  nand NAND_6 (Q_prime, Q, NAND_2_out);
  nand NAND_7 (Q_2, NAND_3_out, Q_prime_2);
  nand NAND_8 (Q_prime_2, Q_2, NAND_4_out);

  // Notes on the sheet:
  //   CLOCK
  //   CLOCK
  //   D-FLIP FLOP USING NAND GATE
  //   JK-FLIP FLOP USING NAND GATE
endmodule
