// Logisim project 24CS104_Experiment_6a.circ as structural Verilog: 1 circuit, main circuit main
module main (
  output out_1,
  output out_2,
  output out_3,
  output out_4
);

  wire button_1_out, clock_1_out, d_ff_1_qn, d_ff_2_qn, d_ff_3_qn, d_ff_4_qn;

  Clock clock_1 (.out(clock_1_out));
  Button button_1 (.out(button_1_out));
  D_Flip_Flop d_ff_1 (
    .clk(clock_1_out), .D(d_ff_1_qn), .Q(out_1), .Qn(d_ff_1_qn), .reset(button_1_out));  // open: preset, en
  D_Flip_Flop d_ff_2 (
    .clk(d_ff_1_qn), .D(d_ff_2_qn), .Q(out_2), .Qn(d_ff_2_qn), .reset(button_1_out));  // open: preset, en
  D_Flip_Flop d_ff_3 (
    .clk(d_ff_2_qn), .D(d_ff_3_qn), .Q(out_3), .Qn(d_ff_3_qn), .reset(button_1_out));  // open: preset, en
  D_Flip_Flop d_ff_4 (
    .clk(d_ff_3_qn), .D(d_ff_4_qn), .Q(out_4), .Qn(d_ff_4_qn), .reset(button_1_out));  // open: preset, en

  // Notes on the sheet:
  //   4 - BIT RIPPLE UP COUNTER
endmodule
