// Logisim project 24CS107_Experiment_1.circ as structural Verilog: 1 circuit, main circuit main
module main (
  input  A,
  input  A_2,
  input  B,
  input  B_2,
  input  A_3,
  input  A_4,
  input  B_3,
  input  B_4,
  input  A_5,
  input  A_6,
  input  B_5,
  input  B_6,
  input  A_7,
  input  A_8,
  input  B_7,
  input  B_8,
  input  A_9,
  input  A_10,
  input  B_9,
  input  B_10,
  input  C,
  input  in_22,
  input  A_11,
  input  A_12,
  input  B_11,
  input  B_12,
  input  C_2,
  input  C_3,
  output A_B__prime,
  output A_prime___B_prime,
  output A_B__prime_2,
  output A_prime_B_prime,
  output A_B,
  output out_34,
  output A_B_2,
  output A_B_3,
  output A__B_C,
  output A_B___A_C,
  output A__B_C_2,
  output A_B___A_C_2
);

  wire and_1_out, and_5_out, and_6_out, not_1_out, not_2_out, not_3_out, not_4_out, or_1_out, or_5_out,
       or_6_out;

  and and_1 (and_1_out, B_10, C);
  or or_1 (or_1_out, B_12, C_3);
  nand nand_1 (A_B__prime, A, B);
  nor nor_1 (A_B__prime_2, A_3, B_3);
  or or_2 (A_B, A_5, B_5);
  and and_2 (A_B_2, A_7, B_7);
  or or_3 (A__B_C, A_10, and_1_out);
  and and_3 (A__B_C_2, A_11, or_1_out);
  not not_1 (not_1_out, A_2);
  not not_2 (not_2_out, B_2);
  not not_3 (not_3_out, A_4);
  not not_4 (not_4_out, B_4);
  or or_4 (out_34, A_6, B_6);
  and and_4 (A_B_3, A_8, B_8);
  or or_5 (or_5_out, A_9, B_9);
  or or_6 (or_6_out, A_9, in_22);
  and and_5 (and_5_out, A_12, B_11);
  and and_6 (and_6_out, A_12, C_2);
  or or_7 (A_prime___B_prime, not_1_out, not_2_out);
  and and_7 (A_prime_B_prime, not_3_out, not_4_out);
  and and_8 (A_B___A_C, or_5_out, or_6_out);
  or or_8 (A_B___A_C_2, and_5_out, and_6_out);

  // Notes on the sheet:
  //   B.C
  //   B+C
  //   Demorgans First Law
  //   Demorgans Second Law
  //   Commutative Property I
  //   Commutative Property II
  //   Distributive Property I
  //   Distributive Property II
  //   A'
  //   B'
  //   A'
  //   B'
  //   A+B
  //   A+C
  //   A+B
  //   (A.B) + (A.C)
endmodule
