// Logisim project 24CS107_Experiment_2.circ as structural Verilog: 1 circuit, main circuit main
module main (
  input  A,
  input  B,
  input  A_2,
  input  B_2,
  input  C,
  output SUM,
  output CARRY,
  output SUM_2,
  output CARRY_2
);

  wire AND_3_out, AND_out, XOR_2_out;

  xor XOR (SUM, A, B);
  xor XOR_2 (XOR_2_out, B_2, C);
  and AND (AND_out, B_2, C);
  buf AND_2 (CARRY, A);  // AND_Gate
  xor XOR_3 (SUM_2, A_2, XOR_2_out);
  and AND_3 (AND_3_out, XOR_2_out, A_2);
  or OR (CARRY_2, AND_3_out, AND_out);

  // Notes on the sheet:
  //   Half-Adder
  //   Full-Adder
endmodule
