// Logisim project 24CS107_Experiment_3.circ as structural Verilog: 1 circuit, main circuit main
module main (
  input  D0,
  input  D1,
  input  D2,
  input  D3,
  input  S1,
  input  S2,
  input  INPUT,
  input  S1_2,
  input  S0,
  output OUTPUT,
  output Y0,
  output Y1,
  output Y2,
  output Y3
);

  wire AND_2_out, AND_3_out, AND_4_out, AND_out, not_1_out, not_2_out, not_3_out, not_4_out;

  not not_1 (not_1_out, S1);
  not not_2 (not_2_out, S2);
  not not_3 (not_3_out, S1_2);
  not not_4 (not_4_out, S0);
  and AND (AND_out, not_1_out, not_2_out, D0);
  and AND_2 (AND_2_out, not_1_out, S2, D1);
  and AND_3 (AND_3_out, S1, S2, D2);
  and AND_4 (AND_4_out, S1, S2, D3);
  and AND_5 (Y0, not_3_out, not_4_out, INPUT);
  and AND_6 (Y1, not_3_out, S0, INPUT);
  and AND_7 (Y2, S1_2, not_4_out, INPUT);
  and AND_8 (Y3, S1_2, S0, INPUT);
  or OR (OUTPUT, AND_out, AND_2_out, AND_3_out, AND_4_out);

  // Notes on the sheet:
  //   1:4 MULTIPLEXER
  //   4:1 MULTIPLEXER
endmodule
